// Logisim project Project3.circ as structural Verilog: 4 circuits, main circuit main
module main (
  input  in_1
);

  wire base_6_counter_1_a, base_6_counter_1_b, base_6_counter_1_c, base_10_counter_1_a, base_10_counter_1_b,
       base_10_counter_1_c, base_10_counter_1_d, base_10_counter_1_v, clock_1_out, display_driver_1_a,
       display_driver_1_b, display_driver_1_c, display_driver_1_d, display_driver_1_e, display_driver_1_f,
       display_driver_1_g, display_driver_2_a, display_driver_2_b, display_driver_2_c, display_driver_2_d,
       display_driver_2_e, display_driver_2_f, display_driver_2_g, not_1_out;

  Clock clock_1 (.out(clock_1_out));
  base_10_counter base_10_counter_1 (
    .Clock(clock_1_out), .X(in_1), .V(base_10_counter_1_v), .D(base_10_counter_1_d), .C(base_10_counter_1_c),
    .B(base_10_counter_1_b), .A(base_10_counter_1_a));
  not not_1 (not_1_out, base_10_counter_1_v);
  display_driver display_driver_1 (
    .b(display_driver_1_b), .a(display_driver_1_a), .f(display_driver_1_f), .g(display_driver_1_g),
    .e(display_driver_1_e), .d(display_driver_1_d), .c(display_driver_1_c), .z(base_10_counter_1_a),
    .y(base_10_counter_1_b), .x(base_10_counter_1_c), .w(base_10_counter_1_d));
  base_6_counter base_6_counter_1 (
    .Clock(not_1_out), .X(in_1), .C(base_6_counter_1_c), .B(base_6_counter_1_b), .A(base_6_counter_1_a));
  _7_Segment_Display u_7_segment_display_1 (
    .g(display_driver_2_g), .f(display_driver_2_f), .a(display_driver_2_a), .b(display_driver_2_b),
    .e(display_driver_2_e), .d(display_driver_2_d), .c(display_driver_2_c));  // open: dp
  display_driver display_driver_2 (
    .b(display_driver_2_b), .a(display_driver_2_a), .f(display_driver_2_f), .g(display_driver_2_g),
    .e(display_driver_2_e), .d(display_driver_2_d), .c(display_driver_2_c), .z(1'b0), .y(base_6_counter_1_a),
    .x(base_6_counter_1_b), .w(base_6_counter_1_c));
  _7_Segment_Display u_7_segment_display_2 (
    .g(display_driver_1_g), .f(display_driver_1_f), .a(display_driver_1_a), .b(display_driver_1_b),
    .e(display_driver_1_e), .d(display_driver_1_d), .c(display_driver_1_c));  // open: dp
endmodule

module base_6_counter (
  input  Clock,
  input  X,
  output C,
  output B,
  output A
);

  wire and_1_out, and_2_out, and_3_out, and_4_out, and_5_out, and_6_out, and_7_out, and_8_out, or_1_out,
       or_2_out, or_3_out, or_4_out;

  J_K_Flip_Flop u_C (.J(1'b1), .clk(Clock), .K(1'b1), .Q(C));  // open: Qn, preset, en, reset
  and and_1 (and_1_out, ~A, C, ~X);  // AND_Gate
  or or_1 (or_1_out, and_1_out, and_2_out);
  and and_2 (and_2_out, A, ~C, X);  // AND_Gate
  and and_3 (and_3_out, C, ~X);  // AND_Gate
  or or_2 (or_2_out, and_3_out, and_4_out);
  and and_4 (and_4_out, ~A, ~C, X);  // AND_Gate
  J_K_Flip_Flop u_B (.J(or_1_out), .clk(Clock), .K(or_2_out), .Q(B));  // open: Qn, preset, en, reset
  and and_5 (and_5_out, B, C, ~X);  // AND_Gate
  or or_3 (or_3_out, and_5_out, and_6_out);
  and and_6 (and_6_out, ~B, ~C, X);  // AND_Gate
  and and_7 (and_7_out, ~C, X);  // AND_Gate
  or or_4 (or_4_out, and_7_out, and_8_out);
  and and_8 (and_8_out, ~B, C, ~X);  // AND_Gate
  J_K_Flip_Flop u_A (.J(or_3_out), .clk(Clock), .K(or_4_out), .Q(A));  // open: Qn, preset, en, reset
endmodule

module base_10_counter (
  input  Clock,
  input  X,
  output D,
  output C,
  output B,
  output A,
  output V
);

  wire and_1_out, and_2_out, and_3_out, and_4_out, and_5_out, and_6_out, and_7_out, and_8_out, and_9_out,
       and_10_out, and_11_out, and_12_out, and_13_out, and_14_out, and_15_out, and_16_out, or_2_out,
       or_3_out, or_4_out, or_5_out, or_6_out, or_7_out;

  or or_1 (V, and_1_out, and_2_out);
  and and_1 (and_1_out, A, D, ~X);  // AND_Gate
  J_K_Flip_Flop u_D (.J(1'b1), .clk(Clock), .K(1'b1), .Q(D));  // open: Qn, preset, en, reset
  and and_2 (and_2_out, ~A, ~B, ~C, ~D, X);  // AND_Gate
  and and_3 (and_3_out, ~A, D, ~X);  // AND_Gate
  and and_4 (and_4_out, B, ~D, X);  // AND_Gate
  and and_5 (and_5_out, A, ~D, X);  // AND_Gate
  and and_6 (and_6_out, D, ~X);  // AND_Gate
  and and_7 (and_7_out, ~A, ~D, X);  // AND_Gate
  or or_2 (or_2_out, and_3_out, and_4_out, and_5_out);
  J_K_Flip_Flop u_C (.J(or_2_out), .clk(Clock), .K(or_3_out), .Q(C));  // open: Qn, preset, en, reset
  or or_3 (or_3_out, and_6_out, and_7_out);
  and and_8 (and_8_out, C, D, ~X);  // AND_Gate
  and and_9 (and_9_out, A, ~D, X);  // AND_Gate
  and and_10 (and_10_out, C, D, ~X);  // AND_Gate
  and and_11 (and_11_out, ~A, ~C, ~D, X);  // AND_Gate
  or or_4 (or_4_out, and_8_out, and_9_out);
  J_K_Flip_Flop u_B (.J(or_4_out), .clk(Clock), .K(or_5_out), .Q(B));  // open: Qn, preset, en, reset
  or or_5 (or_5_out, and_10_out, and_11_out);
  and and_12 (and_12_out, ~B, ~C, ~D, X);  // AND_Gate
  and and_13 (and_13_out, B, C, D, ~X);  // AND_Gate
  and and_14 (and_14_out, ~D, X);  // AND_Gate
  and and_15 (and_15_out, ~B, D, ~X);  // AND_Gate
  and and_16 (and_16_out, ~C, D, ~X);  // AND_Gate
  or or_6 (or_6_out, and_12_out, and_13_out);
  J_K_Flip_Flop u_A (.J(or_6_out), .clk(Clock), .K(or_7_out), .Q(A));  // open: Qn, preset, en, reset
  or or_7 (or_7_out, and_14_out, and_15_out, and_16_out);
endmodule

module display_driver (
  input  z,
  input  y,
  input  x,
  input  w,
  output b,
  output a,
  output f,
  output g,
  output e,
  output d,
  output c
);

  wire and_1_out, and_2_out, and_3_out, and_4_out, nand_1_out, nand_2_out, nand_3_out, nor_1_out, not_1_out,
       not_2_out, not_3_out, not_4_out, not_5_out, or_1_out, or_2_out, or_3_out, or_4_out, xnor_1_out,
       xor_1_out;

  and and_1 (and_1_out, y, w);
  nand nand_1 (nand_1_out, x, w);
  not not_1 (not_1_out, z);
  nand nand_2 (nand_2_out, y, w);
  or or_1 (or_1_out, y, w);
  not not_2 (not_2_out, x);
  nand nand_3 (nand_3_out, x, w);
  or or_2 (or_2_out, x, w);
  not not_3 (not_3_out, x);
  or or_3 (or_3_out, x, w, y);
  or or_4 (or_4_out, z, xnor_1_out);
  xnor xnor_1 (xnor_1_out, x, and_1_out);
  and and_2 (and_2_out, y, not_4_out);
  not not_4 (not_4_out, x);
  and and_3 (and_3_out, y, nand_1_out);
  nor nor_1 (nor_1_out, w, x);
  not not_5 (not_5_out, w);
  and and_4 (and_4_out, not_5_out, x);
  xor xor_1 (xor_1_out, x, y);
  nand nand_4 (a, not_1_out, nand_2_out, or_1_out, not_2_out);
  nand nand_5 (b, y, nand_3_out, or_2_out);
  or or_5 (c, y, not_3_out, w);
  nand nand_6 (d, or_3_out, or_4_out);
  nor nor_2 (e, w, and_2_out);
  or or_6 (f, z, and_3_out, nor_1_out);
  or or_7 (g, z, and_4_out, xor_1_out);
endmodule
